// Logisim project lukas.circ as structural Verilog
module Full_Adder (
  input  A,
  input  B,
  input  CARRY,
  output SUM,
  output CARRY_2
);

  wire and_1_out, and_2_out, xor_1_out;

  xor xor_1 (xor_1_out, A, B);
  and and_1 (and_1_out, A, B);
  and and_2 (and_2_out, xor_1_out, CARRY, CARRY);
  xor xor_2 (SUM, xor_1_out, CARRY);
  or or_1 (CARRY_2, and_1_out, and_2_out);
endmodule

module LK__8_Bit_Adder (
  input  CARRY,
  input  [7:0] A,
  input  [7:0] B,
  output [7:0] SUM,
  output OVERFLOW
);

  wire full_adder_1_carry_2, full_adder_2_carry_2, full_adder_3_carry_2, full_adder_4_carry_2,
       full_adder_5_carry_2, full_adder_6_carry_2, full_adder_7_carry_2;

  Full_Adder full_adder_1 (.A(A[0]), .B(B[0]), .CARRY(CARRY), .SUM(SUM[0]), .CARRY_2(full_adder_1_carry_2));
  Full_Adder full_adder_2 (
    .A(A[1]), .B(B[1]), .CARRY(full_adder_1_carry_2), .SUM(SUM[1]), .CARRY_2(full_adder_2_carry_2));
  Full_Adder full_adder_3 (
    .A(A[2]), .B(B[2]), .CARRY(full_adder_2_carry_2), .SUM(SUM[2]), .CARRY_2(full_adder_3_carry_2));
  Full_Adder full_adder_4 (
    .A(A[3]), .B(B[3]), .CARRY(full_adder_3_carry_2), .SUM(SUM[3]), .CARRY_2(full_adder_4_carry_2));
  Full_Adder full_adder_5 (
    .A(A[4]), .B(B[4]), .CARRY(full_adder_4_carry_2), .SUM(SUM[4]), .CARRY_2(full_adder_5_carry_2));
  Full_Adder full_adder_6 (
    .A(A[5]), .B(B[5]), .CARRY(full_adder_5_carry_2), .SUM(SUM[5]), .CARRY_2(full_adder_6_carry_2));
  Full_Adder full_adder_7 (
    .A(A[6]), .B(B[6]), .CARRY(full_adder_6_carry_2), .SUM(SUM[6]), .CARRY_2(full_adder_7_carry_2));
  Full_Adder full_adder_8 (.A(A[7]), .B(B[7]), .CARRY(full_adder_7_carry_2), .SUM(SUM[7]), .CARRY_2(OVERFLOW));
endmodule

module Incrementor (
  input  [7:0] INPUT,
  output [7:0] OUTPUT,
  output OVERFLOW
);

  LK__8_Bit_Adder lk_8_bit_adder_1 (.CARRY(1'b0), .A(INPUT), .B(8'h1), .SUM(OUTPUT), .OVERFLOW(OVERFLOW));
endmodule
